# Fritzing sketch Connections (saved by Fritzing 0.9.3b)
circuit board: 10cm x 8cm
breadboards: 1

parts:
  IC1 = L293D [package=THT]
  VCC1 = Battery block 9V
  M1 = DC Motor
  M2 = DC Motor
  Part1 = Arduino Mega 2560 (Rev3)

nets:
  N1: IC1.Enable_1, Part1.D10_PWM
  N2: IC1.In_1, Part1.D8_PWM
  N3: IC1.Out_1_(_Controlled_by_Enable_1_), M1.pin_2
  N4: IC1.0V, VCC1.-, Part1.GND
  N5: IC1.Out_2_(_Controlled_by_Enable_1_), M1.pin_1
  N6: IC1.In_2, Part1.D9_PWM
  N7: IC1.+Vmotor, VCC1.+
  N8: IC1.Enable_2, Part1.D11_PWM
  N9: IC1.In_3, Part1.D12_PWM
  N10: IC1.Out_3_(_Controlled_by_Enable_2_), M2.pin_2
  N11: IC1.Out_4_(_Controlled_by_Enable_2_), M2.pin_1
  N12: IC1.In_4, Part1.D13_PWM
  N13: IC1.+V, Part1.5V
